// Digital circuit 2-bit Multiplier.dig as structural Verilog
module _2_bit_Multiplier (
  input  A_0,
  input  A_1,
  input  B_0,
  input  B_1,
  output P_0,
  output P_1,
  output P_2,
  output P_3
);

  wire and_2_out, and_3_out, and_4_out, half_adder_1_carry_out;

  and and_1 (P_0, A_0, B_0);
  and and_2 (and_2_out, A_0, B_1);
  and and_3 (and_3_out, A_1, B_0);
  and and_4 (and_4_out, A_1, B_1);
  Half_Adder half_adder_1 (.A(and_2_out), .B(and_3_out), .Sum(P_1), .Carry_out(half_adder_1_carry_out));
  Half_Adder half_adder_2 (.A(half_adder_1_carry_out), .B(and_4_out), .Sum(P_2), .Carry_out(P_3));
endmodule
