// Digital circuit Half Adder.dig as structural Verilog
module Half_Adder (
  input  A,
  input  B,
  output Sum,
  output Carry_out
);

  xor xor_1 (Sum, A, B);
  and and_1 (Carry_out, A, B);
endmodule
